// Logisim project Practica 1.circ as structural Verilog: 5 circuits, main circuit Memboton
module Visualizador (
  input  A,
  input  B,
  input  C,
  input  Enable,
  output a_2,
  output b_2,
  output c_2,
  output d,
  output e,
  output f,
  output g
);

  // _7448 7448_1: pin names not known; wires that end beside it: B, C, Enable, Enable, Enable, 1'b0, A, f, g, a_2, b_2, c_2, d, e

  // Notes on the sheet:
  //   D
endmodule

module Memboton (
  input  B,
  input  Clock,
  input  R,
  input  E,
  output S
);

  S_R_Flip_Flop s_r_ff_1 (.S(B), .clk(Clock), .R(R), .Q(S), .en(E));  // open: Qn, preset, reset
endmodule

module CodificadorBoton (
  input  PB,
  input  P1,
  input  P2,
  input  P3,
  input  P4,
  output bit0,
  output bit1,
  output bit2
);

  wire not_1_out, not_2_out, not_3_out, or_1_out, or_2_out, or_3_out, or_4_out, or_5_out, or_6_out, or_7_out,
       xor_1_out, xor_2_out;

  or or_1 (or_1_out, P1, PB);
  or or_2 (or_2_out, P1, PB);
  or or_3 (or_3_out, P3, P2);
  or or_4 (or_4_out, PB, P2);
  xor xor_1 (xor_1_out, P1, P3);
  not not_1 (not_1_out, or_5_out);
  or or_5 (or_5_out, P4, or_4_out);
  xor xor_2 (xor_2_out, P3, P2);
  not not_2 (not_2_out, or_6_out);
  or or_6 (or_6_out, P4, or_2_out);
  not not_3 (not_3_out, or_7_out);
  or or_7 (or_7_out, or_3_out, or_1_out);
  and and_1 (bit0, xor_1_out, not_1_out);
  and and_2 (bit1, xor_2_out, not_2_out);
  and and_3 (bit2, P4, not_3_out);
endmodule

module Contador3Bits (
  input  bitUpDown,
  input  Reset,
  input  Clock,
  input  Enable,
  output bit0,
  output bit1,
  output bit2,
  output FinCiclo
);

  wire comparator_1_eq, comparator_1_gt, comparator_2_eq, j_k_ff_1_qn, j_k_ff_3_qn, not_1_out, or_1_out,
       or_2_out, or_3_out, or_4_out, or_5_out, or_6_out;
  wire [1:0] j_k_ff_1_q;
  wire [2:0] j_k_ff_2_q, subtractor_1_out;

  not not_1 (not_1_out, bitUpDown);
  J_K_Flip_Flop j_k_ff_1 (
    .J(bitUpDown), .clk(Clock), .K(bitUpDown), .Q(j_k_ff_1_q[0]), .Qn(j_k_ff_1_qn), .en(Enable),
    .reset(or_1_out));  // open: preset
  or or_1 (or_1_out, Reset, or_6_out);
  J_K_Flip_Flop j_k_ff_2 (
    .J(not_1_out), .clk(Clock), .K(not_1_out), .Q(j_k_ff_2_q[0]), .preset(or_2_out), .en(Enable));  // open: Qn, reset
  or or_2 (or_2_out, Reset, comparator_2_eq);
  J_K_Flip_Flop j_k_ff_3 (
    .J(bitUpDown), .clk(j_k_ff_1_qn), .K(bitUpDown), .Q(j_k_ff_1_q[1]), .Qn(j_k_ff_3_qn), .en(Enable),
    .reset(or_3_out));  // open: preset
  or or_3 (or_3_out, Reset, or_6_out);
  J_K_Flip_Flop j_k_ff_4 (
    .J(not_1_out), .clk(j_k_ff_2_q[0]), .K(not_1_out), .Q(j_k_ff_2_q[1]), .en(Enable), .reset(or_4_out));  // open: Qn, preset
  or or_4 (or_4_out, Reset, comparator_2_eq);
  or or_5 (or_5_out, Reset, or_6_out);
  J_K_Flip_Flop j_k_ff_5 (
    .J(not_1_out), .clk(j_k_ff_2_q[1]), .K(not_1_out), .Q(j_k_ff_2_q[2]), .preset(comparator_2_eq),
    .en(Enable), .reset(Reset));  // open: Qn
  J_K_Flip_Flop j_k_ff_6 (
    .J(bitUpDown), .clk(j_k_ff_3_qn), .K(bitUpDown), .Q(FinCiclo), .en(Enable), .reset(or_5_out));  // open: Qn, preset
  Comparator #(.width(3), .mode("unsigned")) comparator_1 (
    .a({FinCiclo, j_k_ff_1_q}), .b(3'b101), .gt(comparator_1_gt), .eq(comparator_1_eq));  // open: lt
  Comparator #(.width(3), .mode("unsigned")) comparator_2 (
    .a(j_k_ff_2_q), .b(3'b000), .eq(comparator_2_eq));  // open: gt, lt
  or or_6 (or_6_out, comparator_1_eq, comparator_1_gt);
  Subtractor #(.width(3)) subtractor_1 (.a(j_k_ff_2_q), .b(3'b001), .out(subtractor_1_out));  // open: bin, bout
  Multiplexer multiplexer_1 (.in0(subtractor_1_out[0]), .in1(j_k_ff_1_q[0]), .out(bit0), .sel(bitUpDown), .en(Enable));
  Multiplexer multiplexer_2 (.in0(subtractor_1_out[1]), .in1(j_k_ff_1_q[1]), .out(bit1), .sel(bitUpDown), .en(Enable));
  Multiplexer multiplexer_3 (.in0(subtractor_1_out[2]), .in1(FinCiclo), .out(bit2), .sel(bitUpDown), .en(Enable));
endmodule

module Registro3Bits (
  input  Set,
  input  Reset,
  input  D0,
  input  D1,
  input  D2,
  input  Clock,
  input  Enable,
  output Ptb0,
  output Ptb1,
  output Ptb2
);

  wire not_1_out, not_2_out, not_3_out;

  not not_1 (not_1_out, D0);
  not not_2 (not_2_out, D1);
  not not_3 (not_3_out, D2);
  S_R_Flip_Flop s_r_ff_1 (
    .S(D0), .clk(Clock), .R(not_1_out), .Q(Ptb0), .preset(Set), .reset(Reset), .en(Enable));  // open: Qn
  S_R_Flip_Flop s_r_ff_2 (
    .S(D1), .clk(Clock), .R(not_2_out), .Q(Ptb1), .preset(Set), .reset(Reset), .en(Enable));  // open: Qn
  S_R_Flip_Flop s_r_ff_3 (
    .S(D2), .clk(Clock), .R(not_3_out), .Q(Ptb2), .preset(Set), .reset(Reset), .en(Enable));  // open: Qn
endmodule
