// Logisim project circuitoD.circ as structural Verilog
module C (
  input  PB,
  input  P1,
  input  P2,
  input  P3,
  input  P4,
  output BIT1,
  output BIT2,
  output BIT3
);

  wire and_1_out, and_2_out, and_3_out, and_4_out, not_1_out, not_2_out, not_3_out, not_4_out, not_5_out,
       not_6_out, not_7_out, not_8_out, not_9_out, not_10_out, not_11_out, not_12_out, not_13_out,
       not_14_out, not_15_out, not_16_out, not_17_out, not_18_out, not_19_out, not_20_out;

  not not_1 (not_1_out, PB);
  not not_2 (not_2_out, P1);
  not not_3 (not_3_out, P2);
  not not_4 (not_4_out, P4);
  not not_5 (not_5_out, PB);
  not not_6 (not_6_out, P2);
  not not_7 (not_7_out, P3);
  not not_8 (not_8_out, P4);
  not not_9 (not_9_out, PB);
  not not_10 (not_10_out, P1);
  not not_11 (not_11_out, P2);
  not not_12 (not_12_out, P4);
  not not_13 (not_13_out, PB);
  not not_14 (not_14_out, P1);
  not not_15 (not_15_out, P3);
  not not_16 (not_16_out, P4);
  not not_17 (not_17_out, PB);
  not not_18 (not_18_out, P1);
  not not_19 (not_19_out, P2);
  not not_20 (not_20_out, P3);
  and and_1 (and_1_out, not_1_out, not_2_out, not_3_out, P3, not_4_out);
  and and_2 (and_2_out, not_5_out, P1, not_6_out, not_7_out, not_8_out);
  and and_3 (and_3_out, not_9_out, not_10_out, not_11_out, P3, not_12_out);
  and and_4 (and_4_out, not_13_out, not_14_out, P2, not_15_out, not_16_out);
  and and_5 (BIT3, not_17_out, not_18_out, not_19_out, not_20_out, P4);
  or or_1 (BIT1, and_1_out, and_2_out);
  or or_2 (BIT2, and_3_out, and_4_out);
endmodule

module D (
  input  in_1,
  input  in_2,
  input  in_3,
  input  in_4,
  input  in_5,
  input  in_6,
  input  in_7,
  input  in_8,
  input  in_9,
  input  in_10,
  output out_11,
  output out_12,
  output out_13,
  output out_14,
  output out_15,
  output out_16,
  output out_17,
  output out_18
);

  wire and_1_out, and_2_out, clock_1_out, j_k_ff_1_qn, j_k_ff_2_qn, j_k_ff_3_qn, j_k_ff_4_qn, j_k_ff_5_qn,
       j_k_ff_7_qn;

  Clock clock_1 (.out(clock_1_out));
  J_K_Flip_Flop j_k_ff_1 (
    .J(in_6), .clk(clock_1_out), .K(in_6), .Q(out_11), .Qn(j_k_ff_1_qn), .en(in_5), .reset(and_2_out));  // open: preset
  J_K_Flip_Flop j_k_ff_2 (
    .J(in_7), .clk(and_2_out), .K(in_7), .Q(out_18), .Qn(j_k_ff_2_qn), .en(in_8), .reset(and_1_out));  // open: preset
  J_K_Flip_Flop j_k_ff_3 (
    .J(in_6), .clk(j_k_ff_1_qn), .K(in_6), .Q(out_12), .Qn(j_k_ff_3_qn), .en(in_3), .reset(and_2_out));  // open: preset
  J_K_Flip_Flop j_k_ff_4 (
    .J(in_7), .clk(j_k_ff_2_qn), .K(in_7), .Q(out_17), .Qn(j_k_ff_4_qn), .en(in_9), .reset(and_1_out));  // open: preset
  J_K_Flip_Flop j_k_ff_5 (
    .J(in_6), .clk(j_k_ff_3_qn), .K(in_6), .Q(out_13), .Qn(j_k_ff_5_qn), .en(in_1), .reset(and_2_out));  // open: preset
  J_K_Flip_Flop j_k_ff_6 (
    .J(in_7), .clk(j_k_ff_4_qn), .K(in_7), .Q(out_16), .en(in_10), .reset(and_1_out));  // open: Qn, preset
  and and_1 (and_1_out, out_16, out_18);
  J_K_Flip_Flop j_k_ff_7 (
    .J(in_6), .clk(j_k_ff_5_qn), .K(in_6), .Q(out_14), .Qn(j_k_ff_7_qn), .en(in_2), .reset(and_2_out));  // open: preset
  and and_2 (and_2_out, out_15, out_11);
  J_K_Flip_Flop j_k_ff_8 (
    .J(in_6), .clk(j_k_ff_7_qn), .K(in_6), .Q(out_15), .en(in_4), .reset(and_2_out));  // open: Qn, preset
endmodule
