// Logisim project circuitoPrincipal.circ as structural Verilog: 1 circuit, main circuit main
module main (
  input  Enable,
  input  Reset,
  input  Set
);

  wire and_1_out, CLOCK, comparator_1_eq, comparator_1_lt, contador3bits_1_finciclo, contador3bits_2_bit0,
       contador3bits_2_bit1, contador3bits_2_bit2, memboton_1_s, memboton_2_s, memboton_3_s, memboton_4_s,
       memboton_5_s, not_1_out, or_1_out, or_2_out, or_3_out, or_4_out, or_5_out, or_6_out, or_7_out,
       or_8_out, or_9_out, or_10_out, or_11_out, P1_out, P2_out, P3_out, P4_out, PB_out, visualizador_1_a_2,
       visualizador_1_b_2, visualizador_1_c_2, visualizador_1_d, visualizador_1_e, visualizador_1_f,
       visualizador_1_g;
  wire [2:0] codificadorboton_1_bit0, registro3bits_1_ptb0;

  Clock u_Clock (.out(CLOCK));
  Button P4 (.out(P4_out));
  Button P3 (.out(P3_out));
  Button P2 (.out(P2_out));
  Button P1 (.out(P1_out));
  Button PB (.out(PB_out));
  or or_1 (or_1_out, P4_out, P3_out);
  or or_2 (or_2_out, P2_out, P1_out);
  or or_3 (or_3_out, PB_out, P2_out);
  or or_4 (or_4_out, PB_out, P1_out);
  or or_5 (or_5_out, PB_out, P3_out);
  or or_6 (or_6_out, PB_out, P4_out);
  or or_7 (or_7_out, or_1_out, or_2_out);
  or or_8 (or_8_out, or_1_out, or_3_out);
  or or_9 (or_9_out, or_1_out, or_4_out);
  or or_10 (or_10_out, or_2_out, or_5_out);
  or or_11 (or_11_out, or_2_out, or_6_out);
  Memboton memboton_1 (.B(P4_out), .Clock(CLOCK), .R(or_10_out), .E(Enable), .S(memboton_1_s));
  Memboton memboton_2 (.B(P3_out), .Clock(CLOCK), .R(or_11_out), .E(Enable), .S(memboton_2_s));
  Memboton memboton_3 (.B(P2_out), .Clock(CLOCK), .R(or_9_out), .E(Enable), .S(memboton_3_s));
  Memboton memboton_4 (.B(P1_out), .Clock(CLOCK), .R(or_8_out), .E(Enable), .S(memboton_4_s));
  Memboton memboton_5 (.B(PB_out), .Clock(CLOCK), .R(or_7_out), .E(Enable), .S(memboton_5_s));
  CodificadorBoton codificadorboton_1 (
    .PB(memboton_5_s), .P1(memboton_4_s), .P2(memboton_3_s), .P3(memboton_2_s), .P4(memboton_1_s),
    .bit0(codificadorboton_1_bit0[0]), .bit1(codificadorboton_1_bit0[1]), .bit2(codificadorboton_1_bit0[2]));
  not not_1 (not_1_out, comparator_1_eq);
  Comparator #(.width(3), .mode("unsigned")) comparator_1 (
    .a(registro3bits_1_ptb0), .b(codificadorboton_1_bit0), .eq(comparator_1_eq), .lt(comparator_1_lt));  // open: gt
  and and_1 (and_1_out, not_1_out, Enable);
  Contador3Bits contador3bits_1 (
    .bitUpDown(1'b1), .Reset(Reset), .Clock(CLOCK), .Enable(Enable), .FinCiclo(contador3bits_1_finciclo));  // open: bit0, bit1, bit2
  Contador3Bits contador3bits_2 (
    .bitUpDown(comparator_1_lt), .Reset(Reset), .Clock(contador3bits_1_finciclo), .Enable(and_1_out),
    .bit0(contador3bits_2_bit0), .bit1(contador3bits_2_bit1), .bit2(contador3bits_2_bit2));  // open: FinCiclo
  _7_Segment_Display u_7_segment_display_1 (
    .g(visualizador_1_g), .f(visualizador_1_f), .a(visualizador_1_a_2), .b(visualizador_1_b_2),
    .e(visualizador_1_e), .d(visualizador_1_d), .c(visualizador_1_c_2));  // open: dp
  Visualizador visualizador_1 (
    .A(registro3bits_1_ptb0[0]), .B(registro3bits_1_ptb0[1]), .C(registro3bits_1_ptb0[2]), .Enable(Enable),
    .a_2(visualizador_1_a_2), .b_2(visualizador_1_b_2), .c_2(visualizador_1_c_2), .d(visualizador_1_d),
    .e(visualizador_1_e), .f(visualizador_1_f), .g(visualizador_1_g));
  Registro3Bits registro3bits_1 (
    .D0(contador3bits_2_bit0), .D1(contador3bits_2_bit1), .D2(contador3bits_2_bit2), .Set(Set),
    .Reset(Reset), .Clock(CLOCK), .Enable(Enable), .Ptb0(registro3bits_1_ptb0[0]),
    .Ptb1(registro3bits_1_ptb0[1]), .Ptb2(registro3bits_1_ptb0[2]));

  // Other names for the same wires on the sheet: E = Enable; R = Reset; S = Set
endmodule
