// Logisim project Practica2.circ as structural Verilog: 1 circuit, main circuit Prueba
module Prueba (
  input  bit01,
  input  bit11,
  input  bit21,
  input  bit31,
  input  bit02,
  input  bit12,
  input  bit22,
  input  bit32,
  output bit0Suma,
  output bit1Suma,
  output bit2Suma,
  output bit3Suma,
  output Overflow
);

  wire _4_AND_2_p9, _4_AND_p6, _4_AND_p9, _4_AND_p10, _4_AND_p11, _4_OR_p1, _4_OR_p2, _4_OR_p7, _4_OR_p8,
       _4_OR_p9, _4_XOR_p3, _4_XOR_p5;

  // _7486 _4_XOR: pin names not known; wires that end beside it: bit12, bit11, _4_XOR_p3, _4_XOR_p3, _4_XOR_p5, bit1Suma, bit01, bit02, bit0Suma
  // _7408 _4_AND: pin names not known; wires that end beside it: bit02, bit01, _4_XOR_p5, bit12, bit11, _4_AND_p6, _4_XOR_p3, _4_XOR_p5, _4_AND_p9, _4_AND_p10, _4_AND_p11
  // _7432 _4_OR: pin names not known; wires that end beside it: _4_OR_p1, _4_OR_p2, Overflow, _4_OR_p2, _4_AND_p6, _4_AND_p9, _4_OR_p7, _4_OR_p8, _4_OR_p9
  // _7408 _4_AND_2: pin names not known; wires that end beside it: bit22, bit21, _4_OR_p9, bit32, bit31, _4_OR_p1, _4_AND_p10, _4_OR_p7, _4_AND_2_p9
  // _7486 _4_XOR_2: pin names not known; wires that end beside it: bit21, bit22, _4_AND_2_p9, bit32, bit31, _4_AND_p11, _4_OR_p8, _4_AND_2_p9, _4_OR_p7, bit2Suma, _4_AND_p10, _4_AND_p11, bit3Suma
endmodule
