// Logisim project Practica2_Ejemplo.circ as structural Verilog: 4 circuits, main circuit main
module main (
  input  bit01,
  input  bit11,
  input  bit21,
  input  bit31,
  input  bit02,
  input  bit12,
  input  bit22,
  input  bit32,
  output bit0_Suma,
  output bit1Suma,
  output bit2Suma,
  output bit3Suma,
  output Overflow
);

  wire half_adder_1_carry, half_adder_2_carry, half_adder_2_result, half_adder_3_carry, half_adder_3_result,
       half_adder_4_result, half_adder_5_carry, half_adder_6_carry, or_1_out, or_2_out;

  Half_Adder half_adder_1 (.num1(bit01), .num2(bit02), .Result(bit0_Suma), .Carry(half_adder_1_carry));
  Half_Adder half_adder_2 (.num1(bit11), .num2(bit12), .Result(half_adder_2_result), .Carry(half_adder_2_carry));
  Half_Adder half_adder_3 (.num1(bit21), .num2(bit22), .Result(half_adder_3_result), .Carry(half_adder_3_carry));
  Half_Adder half_adder_4 (.num1(bit31), .num2(bit32), .Result(half_adder_4_result));  // open: Carry
  Half_Adder half_adder_5 (
    .num1(half_adder_2_result), .num2(half_adder_1_carry), .Result(bit1Suma), .Carry(half_adder_5_carry));
  or or_1 (or_1_out, half_adder_2_carry, half_adder_5_carry);
  Half_Adder half_adder_6 (.num1(half_adder_3_result), .num2(or_1_out), .Result(bit2Suma), .Carry(half_adder_6_carry));
  or or_2 (or_2_out, half_adder_3_carry, half_adder_6_carry);
  Half_Adder half_adder_7 (.num1(half_adder_4_result), .num2(or_2_out), .Result(bit3Suma), .Carry(Overflow));
endmodule

module Half_Adder (
  input  num1,
  input  num2,
  output Result,
  output Carry
);

  xor xor_1 (Result, num1, num2);
  and and_1 (Carry, num1, num2);
endmodule

module Circuito_con_Integrados (
  input  bit01,
  input  bit11,
  input  bit21,
  input  bit31,
  input  bit02,
  input  bit12,
  input  bit22,
  input  bit32,
  output bit0Suma,
  output bit1Suma,
  output bit2Suma,
  output bit3Suma,
  output Overflow
);

  wire _4_AND_p3, _4_AND_p6, _4_AND_p9, _4_AND_p12, _4_OR_p1, _4_OR_p3, _4_OR_p5, _4_OR_p6, _4_OR_p8,
       _4_XOR_p6, _4_XOR_p9, _4_XOR_p12;

  // _7486 _4_XOR: pin names not known; wires that end beside it: bit01, bit02, bit0Suma, bit11, bit12, _4_XOR_p6, bit21, bit22, _4_XOR_p9, bit31, bit32, _4_XOR_p12, 1'b1
  // _7408 _4_AND: pin names not known; wires that end beside it: bit01, bit02, _4_AND_p3, bit11, bit12, _4_AND_p6, bit21, bit22, _4_AND_p9, bit31, bit32, _4_AND_p12
  // _7432 _4_OR: pin names not known; wires that end beside it: _4_OR_p1, _4_AND_p6, _4_OR_p3, _4_AND_p9, _4_OR_p5, _4_OR_p6, _4_AND_p12, _4_OR_p8, Overflow
  // _7408 _4_AND_2: pin names not known; wires that end beside it: _4_XOR_p6, _4_AND_p3, _4_OR_p1, _4_OR_p3, _4_XOR_p9, _4_OR_p5, _4_XOR_p12, _4_OR_p6, _4_OR_p8
  // _7486 _4_XOR_2: pin names not known; wires that end beside it: 1'b0, _4_XOR_p6, _4_AND_p3, bit1Suma, _4_OR_p3, _4_XOR_p9, bit2Suma, _4_XOR_p12, _4_OR_p6, bit3Suma
endmodule

module Prueba (
  input  bit01,
  input  bit11,
  input  bit21,
  input  bit31,
  input  bit02,
  input  bit12,
  input  bit22,
  input  bit32,
  output bit0Suma,
  output bit1Suma,
  output bit2Suma,
  output bit3Suma
);

  wire _4_AND_2_p6, _4_AND_2_p8, _4_AND_p6, _4_AND_p9, _4_OR_p3, _4_OR_p4, _4_OR_p5, _4_XOR_2_p6, _4_XOR_p3,
       _4_XOR_p5;

  // _7486 _4_XOR: pin names not known; wires that end beside it: bit12, bit11, _4_XOR_p3, _4_XOR_p3, _4_XOR_p5, bit1Suma, bit01, bit02, bit0Suma
  // _7408 _4_AND: pin names not known; wires that end beside it: bit02, bit01, _4_XOR_p5, bit12, bit11, _4_AND_p6, _4_XOR_p3, _4_XOR_p5, _4_AND_p9
  // _7432 _4_OR: pin names not known; wires that end beside it: _4_AND_p6, _4_AND_p9, _4_OR_p3, _4_OR_p4, _4_OR_p5
  // _7408 _4_AND_2: pin names not known; wires that end beside it: bit22, bit21, _4_OR_p5, bit32, bit31, _4_AND_2_p6, _4_OR_p3, _4_AND_2_p8, _4_OR_p4
  // _7486 _4_XOR_2: pin names not known; wires that end beside it: bit21, bit22, _4_AND_2_p8, bit32, bit31, _4_XOR_2_p6, _4_AND_2_p8, _4_OR_p3, bit2Suma, _4_AND_2_p6, _4_XOR_2_p6, bit3Suma
endmodule
