// Logisim project 7448.circ as structural Verilog: 1 circuit, main circuit main
module main (
  input  A,
  input  B,
  input  C,
  input  D,
  input  Enable
);

  wire n7448_1_p8, n7448_1_p9, n7448_1_p10, n7448_1_p11, n7448_1_p12, n7448_1_p13, n7448_1_p14;

  // _7448 7448_1: pin names not known; wires that end beside it: B, C, Enable, Enable, Enable, D, A, n7448_1_p8, n7448_1_p9, n7448_1_p10, n7448_1_p11, n7448_1_p12, n7448_1_p13, n7448_1_p14
  _7_Segment_Display u_7_segment_display_1 (
    .g(n7448_1_p9), .f(n7448_1_p8), .a(n7448_1_p10), .b(n7448_1_p11), .e(n7448_1_p14), .d(n7448_1_p13),
    .c(n7448_1_p12));  // open: dp
endmodule
