// Logisim project Biestables.circ as structural Verilog: 1 circuit, main circuit main
module main (
  input  in_1,
  input  in_2,
  input  in_3,
  input  in_4,
  input  in_5
);

  wire clock_1_out, d_ff_1_q, d_ff_1_qn, j_k_ff_1_q, j_k_ff_1_qn, s_r_ff_1_q, s_r_ff_1_qn;

  Clock clock_1 (.out(clock_1_out));
  D_Flip_Flop d_ff_1 (.clk(clock_1_out), .D(in_2), .Q(d_ff_1_q), .Qn(d_ff_1_qn), .en(in_3));  // open: preset, reset
  S_R_Flip_Flop s_r_ff_1 (
    .S(in_1), .clk(clock_1_out), .R(in_2), .Q(s_r_ff_1_q), .Qn(s_r_ff_1_qn), .en(in_4));  // open: preset, reset
  J_K_Flip_Flop j_k_ff_1 (
    .J(in_1), .clk(clock_1_out), .K(in_2), .Q(j_k_ff_1_q), .Qn(j_k_ff_1_qn), .en(in_5));  // open: preset, reset
endmodule
