// Logisim project Ca2.circ as structural Verilog: 1 circuit, main circuit main
module main (
  input  [4:0] in_1,
  output [4:0] out_2
);

  wire [3:0] not_1_out;

  not not_1 (not_1_out[0], in_1[0]);
  not not_2 (not_1_out[1], in_1[1]);
  not not_3 (not_1_out[2], in_1[2]);
  not not_4 (not_1_out[3], in_1[3]);
  not not_5 (out_2[4], in_1[4]);
  Sumador4bits_main main_1 (.Numero_1(not_1_out), .Numero_2(4'b0001), .Resultado(out_2[3:0]));  // open: Overflow
endmodule
