// Logisim project Contador4bits.circ as structural Verilog: 2 circuits, main circuit main
module main (
  input  Enable,
  input  [3:0] Cota,
  output out_3,
  output out_4,
  output out_5,
  output out_6
);

  wire clock_1_out, comparator_1_eq, j_k_ff_1_qn, j_k_ff_2_qn, j_k_ff_3_qn;

  Clock clock_1 (.out(clock_1_out));
  J_K_Flip_Flop j_k_ff_1 (
    .J(Enable), .clk(clock_1_out), .K(Enable), .Q(out_3), .Qn(j_k_ff_1_qn), .en(Enable),
    .reset(comparator_1_eq));  // open: preset
  J_K_Flip_Flop j_k_ff_2 (
    .J(Enable), .clk(j_k_ff_1_qn), .K(Enable), .Q(out_4), .Qn(j_k_ff_2_qn), .en(Enable),
    .reset(comparator_1_eq));  // open: preset
  Comparator #(.width(4), .mode("unsigned")) comparator_1 (
    .a({out_6, out_5, out_4, out_3}), .b(Cota), .eq(comparator_1_eq));  // open: gt, lt
  J_K_Flip_Flop j_k_ff_3 (
    .J(Enable), .clk(j_k_ff_2_qn), .K(Enable), .Q(out_5), .Qn(j_k_ff_3_qn), .en(Enable),
    .reset(comparator_1_eq));  // open: preset
  J_K_Flip_Flop j_k_ff_4 (
    .J(Enable), .clk(j_k_ff_3_qn), .K(Enable), .Q(out_6), .en(Enable), .reset(comparator_1_eq));  // open: Qn, preset
endmodule

module Contador_Decr (
  input  Enable,
  input  [3:0] Cota,
  output out_3,
  output out_4,
  output out_5,
  output out_6
);

  wire clock_1_out, comparator_1_eq;

  Clock clock_1 (.out(clock_1_out));
  J_K_Flip_Flop j_k_ff_1 (
    .J(Enable), .clk(clock_1_out), .K(Enable), .Q(out_3), .preset(comparator_1_eq), .en(Enable));  // open: Qn, reset
  J_K_Flip_Flop j_k_ff_2 (
    .J(Enable), .clk(out_3), .K(Enable), .Q(out_4), .preset(comparator_1_eq), .en(Enable));  // open: Qn, reset
  Comparator #(.width(4), .mode("unsigned")) comparator_1 (
    .a({out_6, out_5, out_4, out_3}), .b(Cota), .eq(comparator_1_eq));  // open: gt, lt
  J_K_Flip_Flop j_k_ff_3 (
    .J(Enable), .clk(out_4), .K(Enable), .Q(out_5), .preset(comparator_1_eq), .en(Enable));  // open: Qn, reset
  J_K_Flip_Flop j_k_ff_4 (
    .J(Enable), .clk(out_5), .K(Enable), .Q(out_6), .preset(comparator_1_eq), .en(Enable));  // open: Qn, reset
endmodule
