// Logisim project Ejercicio1.circ as structural Verilog: 3 circuits, main circuit main
module main (
);

  Ejercicio1_1 ejercicio1_1_1 ();  // open: d, i, L, D_2, L_2
  Ejercicio1_2 ejercicio1_2_1 ();  // open: A, B, C, M, L

  // Notes on the sheet:
  //   Ejercicio 1
  //   Ejercicio 2
endmodule

module Ejercicio1_1 (
  input  d,
  input  i,
  input  L,
  output D_2,
  output L_2
);

  wire and_1_out, and_2_out, and_3_out, and_4_out, not_1_out, not_2_out, not_3_out;

  not not_1 (not_1_out, i);
  not not_2 (not_2_out, L);
  not not_3 (not_3_out, d);
  and and_1 (and_1_out, d, not_1_out);
  and and_2 (and_2_out, d, not_2_out);
  and and_3 (and_3_out, not_3_out, i);
  and and_4 (and_4_out, i, L);
  or or_1 (D_2, and_1_out, and_2_out);
  or or_2 (L_2, and_3_out, and_4_out);
endmodule

module Ejercicio1_2 (
  input  A,
  input  B,
  input  C,
  output M,
  output L
);

  wire and_1_out, and_2_out, and_3_out, and_4_out, and_5_out, and_6_out, and_7_out, not_1_out, not_2_out,
       not_3_out, not_4_out;

  and and_1 (and_1_out, B, C);
  and and_2 (and_2_out, A, C);
  and and_3 (and_3_out, A, B);
  not not_1 (not_1_out, A);
  not not_2 (not_2_out, A);
  not not_3 (not_3_out, B);
  not not_4 (not_4_out, C);
  or or_1 (M, and_1_out, and_2_out, and_3_out);
  and and_4 (and_4_out, not_1_out, C);
  and and_5 (and_5_out, not_2_out, B);
  and and_6 (and_6_out, A, not_3_out);
  and and_7 (and_7_out, A, not_4_out);
  or or_2 (L, and_4_out, and_5_out, and_6_out, and_7_out);
endmodule
