// Logisim project ExamenEj1.circ as structural Verilog: 3 circuits, main circuit Grey1
module Grey1 (
  input  a,
  input  b,
  input  c,
  output x,
  output y,
  output z
);

  wire and_1_out, and_2_out, and_3_out, and_4_out, not_1_out, not_2_out, not_3_out, not_4_out;

  not not_1 (not_1_out, a);
  not not_2 (not_2_out, b);
  not not_3 (not_3_out, b);
  not not_4 (not_4_out, c);
  and and_1 (and_1_out, not_1_out, b);
  or or_1 (y, and_1_out, and_2_out);
  and and_2 (and_2_out, a, not_2_out);
  and and_3 (and_3_out, not_3_out, c);
  or or_2 (z, and_3_out, and_4_out);
  and and_4 (and_4_out, b, not_4_out);

  assign x = a;
endmodule

module Grey2 (
  input  A,
  input  B,
  input  C,
  output X,
  output Y,
  output Z
);

  wire xor_1_out, xor_2_out, xor_3_out;

  xor xor_1 (xor_1_out, A, C);
  xor xor_2 (xor_2_out, B, C);
  xor xor_3 (xor_3_out, A, B);
  xor xor_4 (Y, xor_1_out, xor_2_out);
  xor xor_5 (Z, xor_1_out, xor_3_out);

  assign X = A;
endmodule

module Grey3 (
  input  A,
  input  B,
  input  C,
  output X,
  output Y,
  output Z
);

  wire or_1_out, or_2_out;

  or or_1 (or_1_out, A, B);
  buf or_2 (or_2_out, C);  // OR_Gate
  and and_1 (Y, or_1_out, or_2_out);

  assign X = A;
endmodule
