// Logisim project Exaxen.circ as structural Verilog: 1 circuit, main circuit ContadorOctal
module ContadorOctal (
  input  Enable,
  input  Reset
);

  wire and_2_out, Clock, registro3bits_1_p1, registro3bits_1_p3, registro3bits_1_p5, registro3bits_2_p4,
       visualizador_1_p1, visualizador_1_p2, visualizador_1_p3, visualizador_1_p4, visualizador_1_p6,
       visualizador_1_p7, visualizador_1_p8, visualizador_1_p9, visualizador_2_p1, visualizador_2_p2,
       visualizador_2_p3, visualizador_2_p4, visualizador_2_p6, visualizador_2_p7, visualizador_2_p8,
       visualizador_2_p9, visualizador_2_p10;

  Clock clock_1 (.out(Clock));
  _7_Segment_Display u_7_segment_display_1 (
    .g(visualizador_1_p2), .f(visualizador_1_p1), .a(visualizador_1_p3), .b(visualizador_1_p4),
    .e(visualizador_1_p9), .d(visualizador_1_p8), .c(visualizador_1_p6));  // open: dp
  // visualizador visualizador_1: pin names not known; wires that end beside it: visualizador_1_p1, visualizador_1_p2, visualizador_1_p3, visualizador_1_p4, 1'b0, visualizador_1_p6, visualizador_1_p7, visualizador_1_p8, visualizador_1_p9
  // registro3bits registro3bits_1: pin names not known; wires that end beside it: registro3bits_1_p1, visualizador_1_p7, registro3bits_1_p3, registro3bits_1_p3, registro3bits_1_p5, Enable, registro3bits_1_p5, Reset, Enable, 1'b1
  and and_1 (registro3bits_1_p1, and_2_out, visualizador_2_p7);
  and and_2 (and_2_out, visualizador_2_p9, registro3bits_2_p4);
  _7_Segment_Display u_7_segment_display_2 (
    .g(visualizador_2_p2), .f(visualizador_2_p1), .a(visualizador_2_p3), .b(visualizador_2_p4),
    .e(visualizador_2_p10), .d(visualizador_2_p8), .c(visualizador_2_p6));  // open: dp
  // visualizador visualizador_2: pin names not known; wires that end beside it: visualizador_2_p1, visualizador_2_p2, visualizador_2_p3, visualizador_2_p4, 1'b0, visualizador_2_p6, visualizador_2_p7, visualizador_2_p8, visualizador_2_p9, visualizador_2_p10
  // registro3bits registro3bits_2: pin names not known; wires that end beside it: Clock, visualizador_2_p7, visualizador_2_p9, registro3bits_2_p4, Enable, registro3bits_2_p4, Reset, Enable, 1'b1
endmodule
