// Logisim project Sumador4bits.circ as structural Verilog: 3 circuits, main circuit main
module main (
  input  [3:0] Numero_1,
  input  [3:0] Numero_2,
  output Overflow,
  output [3:0] Resultado
);

  wire fulladder_1_carry_2, fulladder_2_carry_2, fulladder_3_carry_2;

  FullAdder fulladder_1 (
    .Num1(Numero_1[0]), .Num2(Numero_2[0]), .Carry(1'b0), .Suma(Resultado[0]), .Carry_2(fulladder_1_carry_2));
  FullAdder fulladder_2 (
    .Num1(Numero_1[1]), .Num2(Numero_2[1]), .Carry(fulladder_1_carry_2), .Suma(Resultado[1]),
    .Carry_2(fulladder_2_carry_2));
  FullAdder fulladder_3 (
    .Num1(Numero_1[2]), .Num2(Numero_2[2]), .Carry(fulladder_2_carry_2), .Suma(Resultado[2]),
    .Carry_2(fulladder_3_carry_2));
  FullAdder fulladder_4 (
    .Num1(Numero_1[3]), .Num2(Numero_2[3]), .Carry(fulladder_3_carry_2), .Suma(Resultado[3]),
    .Carry_2(Overflow));
endmodule

module HalfAdder (
  input  num1,
  input  num2,
  output Suma,
  output Carry
);

  xor xor_1 (Suma, num1, num2);
  and and_1 (Carry, num1, num2);
endmodule

module FullAdder (
  input  Num1,
  input  Num2,
  input  Carry,
  output Suma,
  output Carry_2
);

  wire halfadder_1_carry, halfadder_1_suma, halfadder_2_carry;

  HalfAdder halfadder_1 (.num1(Num1), .num2(Num2), .Suma(halfadder_1_suma), .Carry(halfadder_1_carry));
  HalfAdder halfadder_2 (.num1(halfadder_1_suma), .num2(Carry), .Suma(Suma), .Carry(halfadder_2_carry));
  or or_1 (Carry_2, halfadder_1_carry, halfadder_2_carry);
endmodule
